// Logisim project 4 bit ALU circuit.circ as structural Verilog: 2 circuits, main circuit main
module main (
  input  in_1,
  input  in_2,
  input  [3:0] in_3,
  input  [3:0] in_4,
  input  [1:0] in_5,
  output [3:0] out_6
);

  wire memory_1__q, memory_1_q, undriven;
  wire [3:0] adder_1_out, and_1_out, or_1_out, subtractor_1_out;

  memory memory_1 (.in_1(in_1), .in_2(undriven), .Q(memory_1_q), ._Q(memory_1__q));
  Adder #(.width(4)) adder_1 (.a(in_3), .b(in_4), .out(adder_1_out));  // open: cin, cout
  Subtractor #(.width(4)) subtractor_1 (.a(in_3), .b(in_4), .out(subtractor_1_out));  // open: bin, bout
  assign and_1_out = in_3 & in_4;  // AND_Gate and_1, 4 bits wide
  assign or_1_out = in_3 | in_4;  // OR_Gate or_1, 4 bits wide
  Multiplexer #(.select(2), .width(4), .enable("false")) multiplexer_1 (
    .in0(adder_1_out), .in1(subtractor_1_out), .in2(and_1_out), .in3(or_1_out), .out(out_6), .sel(in_5));

  // Notes on the sheet:
  //   ALU Circuit with Add, Subtract, And, Or functions
endmodule

module memory (
  input  in_1,
  input  in_2,
  output Q,
  output _Q
);

  wire clock_1_out, nand_1_out, nand_2_out;

  Clock clock_1 (.out(clock_1_out));
  nand nand_1 (nand_1_out, in_1, clock_1_out);
  nand nand_2 (nand_2_out, clock_1_out, in_2);
  nand nand_3 (Q, nand_1_out, _Q);
  nand nand_4 (_Q, Q, nand_2_out);
endmodule
