// Logisim project RAM.circ as structural Verilog
module memory_4_bits (
  input  _S,
  input  _R,
  input  in_3,
  output Q,
  output _Q
);

  nand nand_1 (Q, _S, _Q);
  nand nand_2 (_Q, Q, _R);
endmodule
