// Logisim project UNIT 3.circ as structural Verilog: 4 circuits, main circuit main
module main (
  input  Cin,
  input  in_2,
  input  in_3,
  input  Input_A,
  input  in_5,
  input  in_6,
  input  in_7,
  input  in_8,
  input  in_9,
  output Overflow,
  output S,
  output S_2,
  output S_3,
  output S_4
);

  wire and_1_out, and_2_out, and_3_out, and_4_out, and_5_out, and_6_out, and_7_out, and_8_out, or_1_out,
       or_2_out, or_3_out, xor_1_out, xor_2_out, xor_3_out, xor_4_out;

  xor xor_1 (xor_1_out, in_5, in_8);
  xor xor_2 (xor_2_out, Input_A, in_9);
  xor xor_3 (xor_3_out, in_3, in_7);
  xor xor_4 (xor_4_out, in_2, in_6);
  xor xor_5 (S_4, xor_1_out, Cin);
  and and_1 (and_1_out, Cin, xor_1_out);
  and and_2 (and_2_out, in_8, in_5);
  xor xor_6 (S_3, xor_2_out, or_1_out);
  and and_3 (and_3_out, or_1_out, xor_2_out);
  and and_4 (and_4_out, in_9, Input_A);
  xor xor_7 (S_2, xor_3_out, or_2_out);
  and and_5 (and_5_out, or_2_out, xor_3_out);
  and and_6 (and_6_out, in_7, in_3);
  xor xor_8 (S, xor_4_out, or_3_out);
  and and_7 (and_7_out, or_3_out, xor_4_out);
  and and_8 (and_8_out, in_6, in_2);
  or or_1 (or_1_out, and_1_out, and_2_out);
  or or_2 (or_2_out, and_3_out, and_4_out);
  or or_3 (or_3_out, and_5_out, and_6_out);
  or or_4 (Overflow, and_7_out, and_8_out);

  // Notes on the sheet:
  //   Input B
  //   Output
endmodule

module ASSIGNMENT_1 (
  input  Cin,
  input  in_2,
  input  in_3,
  input  Input_A,
  input  in_5,
  input  in_6,
  input  in_7,
  input  in_8,
  input  in_9,
  output Overflow,
  output S,
  output S_2,
  output S_3,
  output S_4
);

  wire and_1_out, and_2_out, and_3_out, and_4_out, and_5_out, and_6_out, and_7_out, and_8_out, or_1_out,
       or_2_out, or_3_out, xor_1_out, xor_2_out, xor_3_out, xor_4_out;

  xor xor_1 (xor_1_out, in_5, in_8);
  xor xor_2 (xor_2_out, Input_A, in_9);
  xor xor_3 (xor_3_out, in_3, in_7);
  xor xor_4 (xor_4_out, in_2, in_6);
  xor xor_5 (S_4, xor_1_out, Cin);
  and and_1 (and_1_out, Cin, xor_1_out);
  and and_2 (and_2_out, in_8, in_5);
  xor xor_6 (S_3, xor_2_out, or_1_out);
  and and_3 (and_3_out, or_1_out, xor_2_out);
  and and_4 (and_4_out, in_9, Input_A);
  xor xor_7 (S_2, xor_3_out, or_2_out);
  and and_5 (and_5_out, or_2_out, xor_3_out);
  and and_6 (and_6_out, in_7, in_3);
  xor xor_8 (S, xor_4_out, or_3_out);
  and and_7 (and_7_out, or_3_out, xor_4_out);
  and and_8 (and_8_out, in_6, in_2);
  or or_1 (or_1_out, and_1_out, and_2_out);
  or or_2 (or_2_out, and_3_out, and_4_out);
  or or_3 (or_3_out, and_5_out, and_6_out);
  or or_4 (Overflow, and_7_out, and_8_out);

  // Notes on the sheet:
  //   Input B
  //   ADDER ASSIGNMENT 1
  //   Output
endmodule

module ASSIGNMENT_2 (
  input  Cin,
  input  in_2,
  input  in_3,
  input  Input_A,
  input  in_5,
  input  in_6,
  input  in_7,
  input  in_8,
  input  in_9,
  output Overflow,
  output S,
  output S_2,
  output S_3,
  output S_4
);

  wire and_1_out, and_2_out, and_3_out, and_4_out, and_5_out, and_6_out, and_7_out, and_8_out, not_1_out,
       not_2_out, not_3_out, not_4_out, or_1_out, or_2_out, or_3_out, xor_1_out, xor_2_out, xor_3_out,
       xor_4_out;

  not not_1 (not_1_out, in_6);
  not not_2 (not_2_out, in_7);
  not not_3 (not_3_out, in_8);
  not not_4 (not_4_out, in_9);
  xor xor_1 (xor_1_out, in_5, not_3_out);
  xor xor_2 (xor_2_out, Input_A, not_4_out);
  xor xor_3 (xor_3_out, in_3, not_2_out);
  xor xor_4 (xor_4_out, in_2, not_1_out);
  xor xor_5 (S_4, xor_1_out, Cin);
  and and_1 (and_1_out, Cin, xor_1_out);
  and and_2 (and_2_out, not_3_out, in_5);
  xor xor_6 (S_3, xor_2_out, or_1_out);
  and and_3 (and_3_out, or_1_out, xor_2_out);
  and and_4 (and_4_out, not_4_out, Input_A);
  xor xor_7 (S_2, xor_3_out, or_2_out);
  and and_5 (and_5_out, or_2_out, xor_3_out);
  and and_6 (and_6_out, not_2_out, in_3);
  xor xor_8 (S, xor_4_out, or_3_out);
  and and_7 (and_7_out, or_3_out, xor_4_out);
  and and_8 (and_8_out, not_1_out, in_2);
  or or_1 (or_1_out, and_1_out, and_2_out);
  or or_2 (or_2_out, and_3_out, and_4_out);
  or or_3 (or_3_out, and_5_out, and_6_out);
  or or_4 (Overflow, and_7_out, and_8_out);

  // Notes on the sheet:
  //   Input B
  //   SUBTRACTOR ASSIGNMENT 3
  //   Output
endmodule

module ASSIGNMENT_3 (
  input  [3:0] in_1,
  input  [3:0] in_2,
  input  [1:0] in_3,
  output [3:0] out_4
);

  wire [3:0] adder_1_out, and_1_out, or_1_out, subtractor_1_out;

  Adder #(.width(4)) adder_1 (.a(in_1), .b(in_2), .out(adder_1_out));  // open: cin, cout
  Subtractor #(.width(4)) subtractor_1 (.a(in_1), .b(in_2), .out(subtractor_1_out));  // open: bin, bout
  assign and_1_out = in_1 & in_2;  // AND_Gate and_1, 4 bits wide
  assign or_1_out = in_1 | in_2;  // OR_Gate or_1, 4 bits wide
  Multiplexer #(.select(2), .width(4), .enable("false")) multiplexer_1 (
    .in0(adder_1_out), .in1(subtractor_1_out), .in2(and_1_out), .in3(or_1_out), .out(out_4), .sel(in_3));

  // Notes on the sheet:
  //   ALU ASSIGNMENT 3
endmodule
