// Logisim project system circuit version 2.circ as structural Verilog: 1 circuit, main circuit main
module main (
  input  Reset,
  output Negative,
  output Positive,
  output Zero
);

  wire adder_1_cout, and_1_out, and_2_out, and_3_out, and_4_out, clock_1_out, decoder_1_out1, decoder_1_out2,
       decoder_1_out3, decoder_1_out4, decoder_1_out5, decoder_1_out6, decoder_2_out1, decoder_2_out2,
       decoder_2_out3, decoder_2_out4, decoder_2_out5, decoder_3_out1, decoder_3_out2, not_1_out, not_2_out,
       not_3_out, or_1_out, or_2_out, or_3_out, or_5_out, or_6_out, subtractor_1_bout;
  wire [2:0] demultiplexer_1_out1, demultiplexer_1_out1_3;
  wire [7:0] adder_1_out, and_6_out, controlled_buffer_1_out, controlled_buffer_2_out,
       controlled_buffer_3_out, counter_1_q, demultiplexer_2_out1, demultiplexer_2_out2,
       demultiplexer_2_out3, demultiplexer_2_out4, demultiplexer_2_out5, demultiplexer_2_out6,
       multiplexer_1_out, multiplexer_2_out, or_4_out, ram_1_data, register_1_q, register_2_q, register_3_q,
       register_4_q, register_5_q, register_6_q, register_7_q, subtractor_1_out;
  wire [15:0] demultiplexer_1_out0, demultiplexer_1_out1_2, rom_1_data;

  Clock clock_1 (.out(clock_1_out));
  or or_1 (or_1_out, or_3_out, decoder_1_out2);
  Register #(.trigger("high")) register_1 (
    .D(demultiplexer_2_out5), .en(1'b1), .Q(register_1_q), .clk(decoder_1_out5), .clr(Reset));
  Register #(.trigger("high")) register_2 (
    .D(counter_1_q), .en(1'b1), .Q(register_2_q), .clk(clock_1_out), .clr(Reset));
  assign controlled_buffer_1_out = decoder_1_out2 ? demultiplexer_2_out2 : 8'bz;  // Controlled_Buffer controlled_buffer_1
  not not_1 (not_1_out, or_1_out);
  Counter counter_1 (
    .load(or_1_out), .D(controlled_buffer_1_out), .count(not_1_out), .Q(counter_1_q), .clk(clock_1_out),
    .clr(Reset));  // open: carry
  RAM #(.bus("separate")) ram_1 (
    .addr(register_1_q), .din(controlled_buffer_2_out), .data(ram_1_data), .str(decoder_1_out4), .sel(1'b1),
    .clk(clock_1_out), .ld(and_1_out), .clr(Reset));
  ROM #(.dataWidth(16)) rom_1 (.addr(register_2_q), .data(rom_1_data), .sel(1'b1));
  Demultiplexer #(.width(16), .enable("false")) demultiplexer_1 (
    .out0(demultiplexer_1_out0),
    .out1({demultiplexer_1_out1_2[15:14], demultiplexer_1_out1_3, demultiplexer_1_out1, demultiplexer_1_out1_2[7:0]}),
    .in(rom_1_data), .sel(rom_1_data[15]));
  Demultiplexer #(.select(3), .width(8), .disabled(0), .enable("false")) demultiplexer_2 (
    .out1(demultiplexer_2_out1), .out2(demultiplexer_2_out2), .out3(demultiplexer_2_out3),
    .out4(demultiplexer_2_out4), .out5(demultiplexer_2_out5), .out6(demultiplexer_2_out6), .in(register_7_q),
    .sel(demultiplexer_1_out1));  // open: out0, out7
  assign controlled_buffer_2_out = decoder_1_out4 ? demultiplexer_2_out4 : 8'bz;  // Controlled_Buffer controlled_buffer_2
  Decoder #(.select(3), .enable("false")) decoder_1 (
    .out1(decoder_1_out1), .out2(decoder_1_out2), .out3(decoder_1_out3), .out4(decoder_1_out4),
    .out5(decoder_1_out5), .out6(decoder_1_out6), .sel(demultiplexer_1_out1));  // open: out0, out7
  assign controlled_buffer_3_out = decoder_1_out1 ? demultiplexer_2_out1 : 8'bz;  // Controlled_Buffer controlled_buffer_3
  assign controlled_buffer_3_out = not_2_out ? demultiplexer_1_out0[14:7] : 8'bz;  // Controlled_Buffer controlled_buffer_4
  not not_2 (not_2_out, rom_1_data[15]);
  and and_1 (and_1_out, demultiplexer_1_out1_2[14], clock_1_out);
  Decoder #(.select(3), .enable("false")) decoder_2 (
    .out1(decoder_2_out1), .out2(decoder_2_out2), .out3(decoder_2_out3), .out4(decoder_2_out4),
    .out5(decoder_2_out5), .sel(demultiplexer_1_out1_2[7:5]));  // open: out0, out6, out7
  Register #(.trigger("high")) register_3 (
    .D(demultiplexer_2_out3), .en(1'b1), .Q(register_3_q), .clk(decoder_1_out3), .clr(Reset));
  Register #(.trigger("high")) register_4 (
    .D(controlled_buffer_3_out), .en(1'b1), .Q(register_4_q), .clk(or_2_out), .clr(Reset));
  or or_2 (or_2_out, not_2_out, decoder_1_out1);
  Register #(.trigger("high")) register_5 (.D(ram_1_data), .en(1'b1), .Q(register_5_q), .clk(and_1_out), .clr(Reset));
  and and_2 (and_2_out, decoder_2_out1, Negative);
  and and_3 (and_3_out, decoder_2_out2, Positive);
  and and_4 (and_4_out, decoder_2_out3, Zero);
  Multiplexer #(.width(8), .enable("false")) multiplexer_1 (
    .in0(register_4_q), .in1(register_5_q), .out(multiplexer_1_out), .sel(and_1_out));
  assign controlled_buffer_1_out = or_3_out ? register_6_q : 8'bz;  // Controlled_Buffer controlled_buffer_5
  or or_3 (or_3_out, and_2_out, and_3_out, and_4_out, decoder_2_out4);
  Register #(.trigger("high")) register_6 (
    .D(demultiplexer_2_out6), .en(1'b1), .Q(register_6_q), .clk(decoder_1_out6), .clr(Reset));
  not not_3 (not_3_out, Negative);
  and and_5 (Negative, subtractor_1_bout, decoder_3_out2);
  Adder adder_1 (.a(multiplexer_1_out), .b(register_3_q), .out(adder_1_out), .cout(adder_1_cout));  // open: cin
  Subtractor subtractor_1 (
    .a(register_3_q), .b(multiplexer_1_out), .out(subtractor_1_out), .bout(subtractor_1_bout));  // open: bin
  assign and_6_out = multiplexer_1_out & register_3_q;  // AND_Gate and_6, 8 bits wide
  assign or_4_out = multiplexer_1_out | register_3_q;  // OR_Gate or_4, 8 bits wide
  and and_7 (Positive, not_3_out, or_5_out);
  or or_5 (or_5_out, decoder_3_out2, decoder_3_out1);
  Decoder #(.select(3), .disabled(0), .enable("false")) decoder_3 (
    .out1(decoder_3_out1), .out2(decoder_3_out2), .sel(demultiplexer_1_out1_3));  // open: out0, out3, out4, out5, out6, out7
  not not_4 (Zero, or_6_out);
  or or_6 (or_6_out, register_7_q[7], register_7_q[6], register_7_q[5], register_7_q[4], register_7_q[3], register_7_q[2], register_7_q[1], register_7_q[0]);
  Multiplexer #(.select(3), .width(8), .disabled(0), .enable("false")) multiplexer_2 (
    .in1(adder_1_out), .in2(subtractor_1_out), .in3(and_6_out), .in4(or_4_out), .in5(register_3_q),
    .in6(multiplexer_1_out), .out(multiplexer_2_out), .sel(demultiplexer_1_out1_3));  // open: in0, in7
  Register #(.trigger("falling")) register_7 (
    .D(multiplexer_2_out), .Q(register_7_q), .clk(clock_1_out), .clr(Reset));  // open: en

  // Notes on the sheet:
  //   System Clock
  //   RAM Memory
  //   ROM Memory
  //   contents of rom_1 (hex, n*v repeats v):
  //   0 80 b300 80 8b00 80 b500 ac00 80 b300 cc00 c80 b600 500 b300 d060 400 b200
  //   Extract
  //   Data
  //   Decode Instruction
  //   8 Bit UoPeople Architecture Computer System
  //   Destination Select
  //   D Register
  //   A Register
  //   Memory
  //   Jump
  //   Register
  //   ALU with Add, Subtract, OR and AND Functions
  //   N,P,Z System
  //   Determines if output
  //   value is negative
  //   Positive or Zero
  //   for Jump
endmodule
